// Logisim project Milani_Sommatore 1 bit.circ as structural Verilog: 1 circuit, main circuit main
module main (
  input  A,
  input  B,
  input  A_2,
  input  B_2,
  output S,
  output C,
  output S_2,
  output C_2
);

  xor xor_1 (S, B, A);
  and and_1 (C, A, B);
  Adder #(.width(1)) adder_1 (.a(B_2), .b(A_2), .out(S_2), .cout(C_2));  // open: cin

  // Notes on the sheet:
  //   Milani Francesco 3 AI
endmodule
