// Logisim project Milani_Sommatore 8 bit.circ as structural Verilog: 2 circuits, main circuit main
module main (
  input  A,
  input  B,
  input  C,
  output out_4,
  output out_5
);

  wire and_1_out, and_2_out, and_3_out, and_4_out, and_5_out, and_6_out, not_1_out, not_2_out, not_3_out,
       not_4_out, not_5_out, not_6_out, or_1_out;

  not not_1 (not_1_out, A);
  not not_2 (not_2_out, B);
  and and_1 (and_1_out, A, B, C);
  not not_3 (not_3_out, A);
  not not_4 (not_4_out, C);
  and and_2 (and_2_out, not_1_out, C, not_2_out);
  not not_5 (not_5_out, B);
  not not_6 (not_6_out, C);
  and and_3 (and_3_out, not_5_out, not_6_out, A);
  and and_4 (and_4_out, not_3_out, not_4_out, B);
  and and_5 (and_5_out, A, B, C, C);
  or or_1 (or_1_out, C, B, A);
  and and_6 (and_6_out, A, B, C);
  or or_2 (out_4, and_2_out, and_4_out, and_1_out, and_3_out);
  ExactlyOne xor_1 (.out(out_5), .in1(and_5_out), .in2(or_1_out), .in4(and_6_out));

  // Notes on the sheet:
  //   Milani Francesco 3 AI
  //   Sommatore 8 bit
endmodule

module _2_bit (
  input  C_0,
  input  [1:0] A_B,
  input  [1:0] A_B_2,
  input  [1:0] A_B_3,
  input  [1:0] A_B_4,
  input  [1:0] A_B_5,
  input  [1:0] A_B_6,
  input  [1:0] A_B_7,
  input  [1:0] A_B_8,
  output out_10,
  output out_11,
  output out_12,
  output out_13,
  output out_14,
  output out_15,
  output out_16,
  output out_17,
  output C
);

  wire main_1_out_5, main_2_out_5, main_3_out_5, main_4_out_5, main_5_out_5, main_6_out_5, main_7_out_5;

  main main_1 (.A(A_B[0]), .B(A_B[1]), .C(C_0), .out_4(out_10), .out_5(main_1_out_5));
  main main_2 (.A(A_B_2[0]), .B(A_B_2[1]), .C(main_1_out_5), .out_4(out_11), .out_5(main_2_out_5));
  main main_3 (.A(A_B_3[0]), .B(A_B_3[1]), .C(main_2_out_5), .out_4(out_12), .out_5(main_3_out_5));
  main main_4 (.A(A_B_4[0]), .B(A_B_4[1]), .C(main_3_out_5), .out_4(out_13), .out_5(main_4_out_5));
  main main_5 (.A(A_B_5[0]), .B(A_B_5[1]), .C(main_4_out_5), .out_4(out_14), .out_5(main_5_out_5));
  main main_6 (.A(A_B_6[0]), .B(A_B_6[1]), .C(main_5_out_5), .out_4(out_15), .out_5(main_6_out_5));
  main main_7 (.A(A_B_7[0]), .B(A_B_7[1]), .C(main_6_out_5), .out_4(out_16), .out_5(main_7_out_5));
  main main_8 (.A(A_B_8[0]), .B(A_B_8[1]), .C(main_7_out_5), .out_4(out_17), .out_5(C));
endmodule
