// Logisim project Milani_Sommatore 8 bit_con Display.circ as structural Verilog: 6 circuits, main circuit main
module main (
  input  C_IN,
  input  [7:0] A,
  input  [7:0] B,
  input  C_IN_2,
  input  [7:0] in_5,
  input  [7:0] in_6,
  output [7:0] S,
  output C_OUT,
  output [7:0] out_9,
  output out_10
);

  wire [3:0] splitter_8_2_1_out_2, splitter_8_2_1_out_3, splitter_8_2_2_out_2, splitter_8_2_2_out_3,
       splitter_8_2_3_out_2, splitter_8_2_3_out_3;

  Splitter_8_2 splitter_8_2_1 (.in_1(A), .out_2(splitter_8_2_1_out_2), .out_3(splitter_8_2_1_out_3));
  Hex_Digit_Display hex_digit_display_1 (.value(splitter_8_2_1_out_2));  // open: dp
  Hex_Digit_Display hex_digit_display_2 (.value(splitter_8_2_1_out_3));  // open: dp
  Hex_Digit_Display hex_digit_display_3 (.value(in_5[3:0]));  // open: dp
  Hex_Digit_Display hex_digit_display_4 (.value(in_5[7:4]));  // open: dp
  Hex_Digit_Display hex_digit_display_5 (.value(splitter_8_2_2_out_3));  // open: dp
  Hex_Digit_Display hex_digit_display_6 (.value(splitter_8_2_2_out_2));  // open: dp
  Splitter_8_2 splitter_8_2_2 (.in_1(B), .out_2(splitter_8_2_2_out_2), .out_3(splitter_8_2_2_out_3));
  Hex_Digit_Display hex_digit_display_7 (.value(in_6[7:4]));  // open: dp
  Hex_Digit_Display hex_digit_display_8 (.value(in_6[3:0]));  // open: dp
  Sommatore_8_bit sommatore_8_bit_1 (.C_IN(C_IN), .S(S), .C_OUT(C_OUT), .A(A), .B(B));
  Adder adder_1 (.a(in_5), .b(in_6), .out(out_9), .cin(C_IN_2), .cout(out_10));
  Hex_Digit_Display hex_digit_display_9 (.value(splitter_8_2_3_out_3));  // open: dp
  Hex_Digit_Display hex_digit_display_10 (.value(splitter_8_2_3_out_2));  // open: dp
  Splitter_8_2 splitter_8_2_3 (.in_1(S), .out_2(splitter_8_2_3_out_2), .out_3(splitter_8_2_3_out_3));
  Hex_Digit_Display hex_digit_display_11 (.value(out_9[3:0]));  // open: dp
  Hex_Digit_Display hex_digit_display_12 (.value(out_9[7:4]));  // open: dp

  // Notes on the sheet:
  //   Milani Francesco 3 AI
  //   A
  //   A
  //   B
  //   B
  //    Sommatore 8 bit con display
  //   S
  //   S
endmodule

module Sommatore_2_bit (
  input  A,
  input  B,
  input  C_IN,
  output S,
  output C_OUT
);

  wire and_1_out, and_2_out, and_3_out, and_4_out, and_5_out, and_6_out, and_7_out, not_1_out, not_2_out,
       not_3_out, not_4_out, not_5_out, not_6_out;

  not not_1 (not_1_out, A);
  not not_2 (not_2_out, B);
  not not_3 (not_3_out, A);
  not not_4 (not_4_out, C_IN);
  not not_5 (not_5_out, B);
  not not_6 (not_6_out, C_IN);
  and and_1 (and_1_out, not_1_out, not_2_out, C_IN);
  and and_2 (and_2_out, not_3_out, B, not_4_out);
  and and_3 (and_3_out, A, not_5_out, not_6_out);
  and and_4 (and_4_out, A, B, C_IN);
  and and_5 (and_5_out, A, B);
  and and_6 (and_6_out, A, C_IN);
  and and_7 (and_7_out, B, C_IN);
  or or_1 (S, and_1_out, and_2_out, and_3_out, and_4_out);
  or or_2 (C_OUT, and_5_out, and_6_out, and_7_out);

  // Notes on the sheet:
  //   Milani Francesco 3 AI
  //   Sommatore 2 bit
endmodule

module Sommatore_8_bit (
  input  C_IN,
  input  [7:0] B,
  input  [7:0] A,
  output [7:0] S,
  output C_OUT
);

  wire sommatore_2_bit_1_c_out, sommatore_2_bit_2_c_out, sommatore_2_bit_3_c_out, sommatore_2_bit_4_c_out,
       sommatore_2_bit_5_c_out, sommatore_2_bit_6_c_out, sommatore_2_bit_7_c_out;
  wire [3:0] splitter_8_2_1_out_2, splitter_8_2_1_out_3, splitter_8_2_2_out_2, splitter_8_2_2_out_3;

  Hex_Digit_Display hex_digit_display_1 (.value(splitter_8_2_1_out_3));  // open: dp
  Splitter_8_2 splitter_8_2_1 (.in_1(A), .out_2(splitter_8_2_1_out_2), .out_3(splitter_8_2_1_out_3));
  Hex_Digit_Display hex_digit_display_2 (.value(splitter_8_2_1_out_2));  // open: dp
  Hex_Digit_Display hex_digit_display_3 (.value(splitter_8_2_2_out_3));  // open: dp
  Splitter_8_2 splitter_8_2_2 (.in_1(B), .out_2(splitter_8_2_2_out_2), .out_3(splitter_8_2_2_out_3));
  Hex_Digit_Display hex_digit_display_4 (.value(splitter_8_2_2_out_2));  // open: dp
  Sommatore_2_bit sommatore_2_bit_1 (.A(A[0]), .B(B[0]), .C_IN(C_IN), .S(S[0]), .C_OUT(sommatore_2_bit_1_c_out));
  Sommatore_2_bit sommatore_2_bit_2 (
    .A(B[1]), .B(A[1]), .C_IN(sommatore_2_bit_1_c_out), .S(S[1]), .C_OUT(sommatore_2_bit_2_c_out));
  Sommatore_2_bit sommatore_2_bit_3 (
    .A(B[2]), .B(A[2]), .C_IN(sommatore_2_bit_2_c_out), .S(S[2]), .C_OUT(sommatore_2_bit_3_c_out));
  Sommatore_2_bit sommatore_2_bit_4 (
    .A(A[3]), .B(B[3]), .C_IN(sommatore_2_bit_3_c_out), .S(S[3]), .C_OUT(sommatore_2_bit_4_c_out));
  Sommatore_2_bit sommatore_2_bit_5 (
    .A(A[4]), .B(B[4]), .C_IN(sommatore_2_bit_4_c_out), .S(S[4]), .C_OUT(sommatore_2_bit_5_c_out));
  Sommatore_2_bit sommatore_2_bit_6 (
    .A(A[5]), .B(B[5]), .C_IN(sommatore_2_bit_5_c_out), .S(S[5]), .C_OUT(sommatore_2_bit_6_c_out));
  Sommatore_2_bit sommatore_2_bit_7 (
    .A(A[6]), .B(B[6]), .C_IN(sommatore_2_bit_6_c_out), .S(S[6]), .C_OUT(sommatore_2_bit_7_c_out));
  Sommatore_2_bit sommatore_2_bit_8 (.A(A[7]), .B(B[7]), .C_IN(sommatore_2_bit_7_c_out), .S(S[7]), .C_OUT(C_OUT));

  // Notes on the sheet:
  //   Milani Francesco 3 AI
  //    Sommatore 8 bit con display
endmodule

module Splitter_8_4 (
  input  [7:0] in_1,
  output [1:0] out_2,
  output [1:0] out_3,
  output [1:0] out_4,
  output [1:0] out_5
);


  assign out_2 = in_1[1:0];
  assign out_3 = in_1[3:2];
  assign out_4 = in_1[5:4];
  assign out_5 = in_1[7:6];

  // Notes on the sheet:
  //   Milani Francesco 3 AI
  //   Splitter 8 bit-4 bit
endmodule

module Splitter_4_2 (
  input  [1:0] in_1,
  input  [1:0] in_2,
  input  [1:0] in_3,
  input  [1:0] in_4,
  output [3:0] out_5,
  output [3:0] out_6
);


  assign out_5 = {in_2, in_1};
  assign out_6 = {in_4, in_3};

  // Notes on the sheet:
  //   Milani Francesco 3 AI
  //   Splitter 4 bit-2 bit
endmodule

module Splitter_8_2 (
  input  [7:0] in_1,
  output [3:0] out_2,
  output [3:0] out_3
);

  wire [1:0] splitter_8_4_1_out_2, splitter_8_4_1_out_3, splitter_8_4_1_out_4, splitter_8_4_1_out_5;

  Splitter_8_4 splitter_8_4_1 (
    .in_1(in_1), .out_2(splitter_8_4_1_out_2), .out_3(splitter_8_4_1_out_3), .out_4(splitter_8_4_1_out_4),
    .out_5(splitter_8_4_1_out_5));
  Splitter_4_2 splitter_4_2_1 (
    .in_1(splitter_8_4_1_out_2), .in_2(splitter_8_4_1_out_3), .in_3(splitter_8_4_1_out_4),
    .in_4(splitter_8_4_1_out_5), .out_5(out_2), .out_6(out_3));

  // Notes on the sheet:
  //   Milani Francesco 3 AI
  //   Splitter 8 bit-2 bit
endmodule
